# Fritzing sketch diagram (saved by Fritzing 0.9.0b)
circuit board: 8.46667cm x 5.64444cm
breadboards: 1

parts:
  UNO = Arduino Uno (Rev3)
  Playback = LED - 5mm [color="Green (570nm)" package="5 mm [THT]"]
  Recording = LED - 5mm [color="Red (633nm)" package="5 mm [THT]"]
  Output = LED - 5mm [color="Yellow (585nm)" package="5 mm [THT]"]
  R1 = Resistor [tolerance=±5% resistance=1k package=THT]
  R2 = Resistor [tolerance=±5% resistance=1k package=THT]
  S1 = Pushbutton [package="[THT]"]
  R4 = Resistor [tolerance=±5% resistance=10k package=THT]
  R5 = Resistor [tolerance=±5% resistance=220 package=THT]
  R6 = Resistor [tolerance=±5% resistance=1k package=THT]
  R3 = Resistor [tolerance=±5% resistance=1k package=THT]
  SPKR1 = Loudspeaker

nets:
  N1: UNO.D11_PWM/MOSI, R2.Pin_0
  N2: UNO.D12/MISO, R3.Pin_1
  N3: UNO.D13/SCK, R1.Pin_0
  GND: UNO.GND, Playback.cathode, Recording.cathode, Output.cathode, R4.Pin_0, SPKR1.pin1
  N4: UNO.D2, S1.Pin_1, S1.Pin_2, R4.Pin_1
  N5: UNO.D5_PWM, R6.Pin_0
  N6: UNO.5V, R5.Pin_0
  N7: Playback.anode, R3.Pin_0
  N8: Recording.anode, R2.Pin_1
  N9: Output.anode, R1.Pin_1
  N10: S1.Pin_3, S1.Pin_4, R5.Pin_1
  N11: R6.Pin_1, SPKR1.pin2

notes:
  (Battery powered AMP/Speaker)
